// Logisim project coders.circ as structural Verilog: 3 circuits, main circuit main
module main (
  input  in_1,
  input  in_2,
  output out_3,
  output out_4,
  output out_5,
  output out_6,
  output out_7,
  output out_8
);

  wire not_1_out, not_2_out;

  not not_1 (not_1_out, in_1);
  not not_2 (not_2_out, in_2);
  and and_1 (out_3, not_1_out, not_2_out);
  and and_2 (out_5, in_1, not_2_out);
  and and_3 (out_6, not_1_out, in_2);
  and and_4 (out_8, in_1, in_2);
  or or_1 (out_4, out_5, out_8);
  or or_2 (out_7, out_6, out_8);
endmodule

module decoder (
  input  in_1,
  input  in_2,
  output out_3,
  output out_4,
  output out_5,
  output out_6
);

  wire not_1_out, not_2_out;

  not not_1 (not_1_out, in_1);
  not not_2 (not_2_out, in_2);
  and and_1 (out_3, not_1_out, not_2_out);
  and and_2 (out_4, in_1, not_2_out);
  and and_3 (out_5, not_1_out, in_2);
  and and_4 (out_6, in_1, in_2);
endmodule

module encoder (
  input  in_1,
  input  in_2,
  input  in_3,
  input  in_4,
  output out_5,
  output out_6
);

  or or_1 (out_5, in_2, in_4);
  or or_2 (out_6, in_3, in_4);
endmodule
