// Logisim project dist-2.circ as structural Verilog: 1 circuit, main circuit main
module main (
  input  in_1,
  input  in_2,
  input  in_3,
  output out_4,
  output out_5
);

  wire and_1_out, or_1_out, or_2_out;

  and and_1 (and_1_out, in_2, in_3);
  or or_1 (or_1_out, in_2, in_1);
  or or_2 (or_2_out, in_3, in_1);
  or or_3 (out_4, in_1, and_1_out);
  and and_2 (out_5, or_1_out, or_2_out);
endmodule
