// Logisim project myFirst.circ as structural Verilog: 1 circuit, main circuit myFirst
module myFirst (
  input  in_1,
  output out_2
);

  wire nand_1_out, nor_1_out, not_1_out;

  not nand_1 (nand_1_out, in_1);  // NAND_Gate
  not nor_1 (nor_1_out, nand_1_out);  // NOR_Gate
  not not_1 (not_1_out, nor_1_out);
  buf xor_1 (out_2, not_1_out);  // XOR_Gate
endmodule
