// Logisim project lab2-part1.circ as structural Verilog: 4 circuits, main circuit mux-2
module mux_2 (
  input  in_1,
  input  select,
  input  in_2,
  output out
);

  wire AND_1_out, AND_2_out;

  and AND_1 (AND_1_out, in_1, ~select);  // AND_Gate
  and AND_2 (AND_2_out, select, in_2);
  or OR (out, AND_1_out, AND_2_out);

  // Notes on the sheet:
  //   Activating no selection selects in_1
  //   Activating selection selects in_2
endmodule

module mux_4i (
  input  in_1,
  input  in_2,
  input  select_1,
  input  select_2,
  input  in_3,
  input  in_4,
  output out
);

  wire AND_1_out, AND_2_out, AND_3_out, AND_4_out;

  and AND_1 (AND_1_out, in_1, ~select_1, ~select_2);  // AND_Gate
  and AND_2 (AND_2_out, in_2, select_1, ~select_2);  // AND_Gate
  and AND_3 (AND_3_out, ~select_1, select_2, in_3);  // AND_Gate
  and AND_4 (AND_4_out, select_1, select_2, in_4);
  or OR (out, AND_1_out, AND_2_out, AND_3_out, AND_4_out);

  // Notes on the sheet:
  //   Activating no selection selects in_1
  //   Activating select_1 and not select_2 selects in_2
  //   Activating not select_1 and select_2 selects in_3
  //   Activating select_1 and select_2 selects in_4
endmodule

// mux_4i
module mux_4ii (
  input  in_1,
  input  in_2,
  input  select_1,
  input  select_2,
  input  in_3,
  input  in_4,
  output out
);

  wire mux_2_2_out, mux_2_out;

  mux_2 mux_2 (.in_1(in_1), .select(select_1), .in_2(in_2), .out(mux_2_out));
  mux_2 mux_2_2 (.in_1(in_3), .select(select_1), .in_2(in_4), .out(mux_2_2_out));
  mux_2 mux_2_3 (.in_1(mux_2_out), .select(select_2), .in_2(mux_2_2_out), .out(out));

  // Notes on the sheet:
  //   Activating no selection selects in_1
  //   Activating select_1 and not select_2 selects in_2
  //   Activating not select_1 and select_2 selects in_3
  //   Activating select_1 and select_2 selects in_4
endmodule

module mux_2_6 (
  input  [5:0] in_1,
  input  select,
  input  [5:0] in_2,
  output [5:0] out
);

  wire AND_1_1_out, AND_1_2_out, AND_1_3_out, AND_1_4_out, AND_1_5_out, AND_1_6_out, AND_2_1_out,
       AND_2_2_out, AND_2_3_out, AND_2_4_out, AND_2_5_out, AND_2_6_out;

  and AND_1_6 (AND_1_6_out, in_1[5], ~select);  // AND_Gate
  or OR_6 (out[5], AND_1_6_out, AND_2_6_out);
  and AND_1_5 (AND_1_5_out, in_1[4], ~select);  // AND_Gate
  and AND_1_4 (AND_1_4_out, in_1[3], ~select);  // AND_Gate
  and AND_1_3 (AND_1_3_out, in_1[2], ~select);  // AND_Gate
  or OR_5 (out[4], AND_1_5_out, AND_2_5_out);
  and AND_1_2 (AND_1_2_out, in_1[1], ~select);  // AND_Gate
  or OR_4 (out[3], AND_1_4_out, AND_2_4_out);
  and AND_2_6 (AND_2_6_out, ~select, in_2[5]);  // AND_Gate
  and AND_1_1 (AND_1_1_out, in_1[0], ~select);  // AND_Gate
  and AND_2_5 (AND_2_5_out, ~select, in_2[4]);  // AND_Gate
  or OR_3 (out[2], AND_1_3_out, AND_2_3_out);
  and AND_2_4 (AND_2_4_out, ~select, in_2[3]);  // AND_Gate
  or OR_2 (out[1], AND_1_2_out, AND_2_2_out);
  and AND_2_3 (AND_2_3_out, ~select, in_2[2]);  // AND_Gate
  and AND_2_2 (AND_2_2_out, ~select, in_2[1]);  // AND_Gate
  and AND_2_1 (AND_2_1_out, ~select, in_2[0]);  // AND_Gate
  or OR_1 (out[0], AND_1_1_out, AND_2_1_out);
endmodule
