// Logisim project lab2-part2.circ as structural Verilog: 2 circuits, main circuit fa-1
module fa_1 (
  input  in_1,
  input  in_2,
  input  carry_in,
  output sum,
  output carry_out
);

  wire a_b_2_out, a_b_out, carry__a_b_out;

  and a_b (a_b_out, in_1, in_2);
  or OR_carry (carry_out, a_b_out, carry__a_b_out);
  xor a_b_2 (a_b_2_out, in_1, in_2);
  and carry__a_b (carry__a_b_out, carry_in, a_b_2_out);
  xor a_b__c (sum, a_b_2_out, carry_in);
endmodule

module alu_1 (
  input  select_1,
  input  select_2,
  input  in_1,
  input  in_2,
  input  carry_in,
  output out,
  output carry_out
);

  wire AND_out, fa_1_sum, OR_out;

  fa_1 fa_1 (.in_1(in_1), .in_2(in_2), .carry_in(carry_in), .carry_out(carry_out), .sum(fa_1_sum));
  and AND (AND_out, in_1, in_2);
  or OR (OR_out, in_2, in_1);
  mux_4i mux_4i (
    .in_1(AND_out), .in_2(OR_out), .select_1(select_1), .select_2(select_2), .in_3(fa_1_sum), .out(out));  // open: in_4

  // Notes on the sheet:
  //   Activating select_1 will give the OR of in_1 and in_2
  //   Activating no selection gives the AND of in_1 and in_2
  //   Activating select_2 will give the ADD of in_1 and in_2
  //   Please not that the assignment spec only includes 3 operations for the ALU
  //   Thus, activating both select_1 and select_2 will give an error for the output
endmodule
