// Logisim project lab2-part3.circ as structural Verilog: 1 circuit, main circuit fa-4
module fa_4 (
  input  [3:0] in_1,
  input  [3:0] in_2,
  input  carry_in,
  output carry_out,
  output [3:0] out
);

  wire fa_1_2_carry_out, fa_1_3_carry_out, fa_1_carry_out;

  fa_1 fa_1 (.in_1(in_1[0]), .in_2(in_2[0]), .carry_in(carry_in), .carry_out(fa_1_carry_out), .sum(out[0]));
  fa_1 fa_1_2 (.in_1(in_1[1]), .in_2(in_2[1]), .carry_in(fa_1_carry_out), .carry_out(fa_1_2_carry_out), .sum(out[1]));
  fa_1 fa_1_3 (.in_1(in_1[2]), .in_2(in_2[2]), .carry_in(fa_1_2_carry_out), .carry_out(fa_1_3_carry_out), .sum(out[2]));
  fa_1 fa_1_4 (.in_1(in_1[3]), .in_2(in_2[3]), .carry_in(fa_1_3_carry_out), .carry_out(carry_out), .sum(out[3]));
endmodule
