// Logisim project lab3.circ as structural Verilog: 3 circuits, main circuit alu-1bit-sub
module alu_1bit_sub (
  input  Binvert,
  input  Cin,
  input  Op2,
  input  Op1,
  input  A,
  input  B,
  output Result,
  output Cout
);

  wire ADDER__1bit_sum, AND_out, MUX__2_way_out, not_1_out, OR_out;

  mux_2 MUX__2_way (.in_1(B), .select(Binvert), .in_2(not_1_out), .out(MUX__2_way_out));
  not not_1 (not_1_out, B);
  and AND (AND_out, A, MUX__2_way_out);
  or OR (OR_out, A, MUX__2_way_out);
  fa_1 ADDER__1bit (.in_1(A), .in_2(MUX__2_way_out), .carry_in(Cin), .carry_out(Cout), .sum(ADDER__1bit_sum));
  mux_4i MUX__4_way (
    .in_1(AND_out), .in_2(OR_out), .select_1(Op1), .select_2(Op2), .in_3(ADDER__1bit_sum), .in_4(A),
    .out(Result));

  // Notes on the sheet:
  //   Please note that the assignment spec only includes 3 operations for the ALU.
  //   Thus, activating both OP1 and OP2 will ouput the state of A to avoid errors.
endmodule

// ALU (1bit)
module alu_1bit_slt (
  input  Ainvert,
  input  Binvert,
  input  Cin,
  input  Op2,
  input  Op1,
  input  A,
  input  B,
  input  Less,
  output Result,
  output Set,
  output Overflow,
  output Cout
);

  wire ADDER__1bit_sum, AND_out, MUX__2_way_2_out, MUX__2_way_out, not_1_out, not_2_out, OR_out;

  not not_1 (not_1_out, A);
  not not_2 (not_2_out, B);
  mux_2 MUX__2_way (.in_1(A), .select(Ainvert), .in_2(not_1_out), .out(MUX__2_way_out));
  mux_2 MUX__2_way_2 (.in_1(B), .select(Binvert), .in_2(not_2_out), .out(MUX__2_way_2_out));
  and AND (AND_out, MUX__2_way_out, MUX__2_way_2_out);
  or OR (OR_out, MUX__2_way_out, MUX__2_way_2_out);
  fa_1 ADDER__1bit (
    .in_1(MUX__2_way_out), .in_2(MUX__2_way_2_out), .carry_in(Cin), .carry_out(Cout), .sum(ADDER__1bit_sum));
  xor XOR (Overflow, Cin, Cout);
  mux_4i MUX__4_way (
    .in_1(AND_out), .in_2(OR_out), .select_1(Op1), .select_2(Op2), .in_3(ADDER__1bit_sum), .in_4(Less),
    .out(Result));
  xor XOR_2 (Set, ADDER__1bit_sum, Overflow);
endmodule

module alu_6bit_mips (
  input  [5:0] A,
  input  [5:0] B,
  input  Ainvert,
  input  Bnegate,
  input  Op2,
  input  Op1,
  input  in_7,
  input  in_8,
  input  in_9,
  input  in_10,
  input  in_11,
  output Zero,
  output Overflow,
  output Cout,
  output [5:0] Result
);

  wire alu_1bit_slt_1_cout, alu_1bit_slt_2_cout, alu_1bit_slt_3_cout, alu_1bit_slt_4_cout,
       alu_1bit_slt_5_cout, alu_1bit_slt_6_set, OR_out;

  alu_1bit_slt alu_1bit_slt_1 (
    .A(A[0]), .B(B[0]), .Less(alu_1bit_slt_6_set), .Ainvert(Ainvert), .Binvert(Bnegate), .Cin(Bnegate),
    .Op2(Op2), .Op1(Op1), .Cout(alu_1bit_slt_1_cout), .Result(Result[0]));  // open: Set, Overflow
  alu_1bit_slt alu_1bit_slt_2 (
    .A(A[1]), .B(B[1]), .Less(in_7), .Ainvert(Ainvert), .Binvert(Bnegate), .Cin(alu_1bit_slt_1_cout),
    .Op2(Op2), .Op1(Op1), .Cout(alu_1bit_slt_2_cout), .Result(Result[1]));  // open: Set, Overflow
  alu_1bit_slt alu_1bit_slt_3 (
    .A(A[2]), .B(B[2]), .Less(in_8), .Ainvert(Ainvert), .Binvert(Bnegate), .Cin(alu_1bit_slt_2_cout),
    .Op2(Op2), .Op1(Op1), .Cout(alu_1bit_slt_3_cout), .Result(Result[2]));  // open: Set, Overflow
  alu_1bit_slt alu_1bit_slt_4 (
    .A(A[3]), .B(B[3]), .Less(in_9), .Ainvert(Ainvert), .Binvert(Bnegate), .Cin(alu_1bit_slt_3_cout),
    .Op2(Op2), .Op1(Op1), .Cout(alu_1bit_slt_4_cout), .Result(Result[3]));  // open: Set, Overflow
  alu_1bit_slt alu_1bit_slt_5 (
    .A(A[4]), .B(B[4]), .Less(in_10), .Ainvert(Ainvert), .Binvert(Bnegate), .Cin(alu_1bit_slt_4_cout),
    .Op2(Op2), .Op1(Op1), .Cout(alu_1bit_slt_5_cout), .Result(Result[4]));  // open: Set, Overflow
  alu_1bit_slt alu_1bit_slt_6 (
    .A(A[5]), .B(B[5]), .Less(in_11), .Ainvert(Ainvert), .Binvert(Bnegate), .Cin(alu_1bit_slt_5_cout),
    .Op2(Op2), .Op1(Op1), .Cout(Cout), .Result(Result[5]), .Set(alu_1bit_slt_6_set), .Overflow(Overflow));
  or OR (OR_out, Result[0], Result[1], Result[2], Result[3], Result[4], Result[5]);
  not not_1 (Zero, OR_out);
endmodule
