// Logisim project cla.circ as structural Verilog: 5 circuits, main circuit CLA-PG1
// CLA 1bit
module CLA_PG1 (
  input  Cin,
  input  A,
  input  B,
  output S,
  output P,
  output G,
  output Cout
);

  wire a_prime_b_prime_cin_out, a_prime_bcin_prime_out, ab_prime_cin_prime_out, abcin_out, acin_out, bcin_out;

  and abcin (abcin_out, A, B, Cin);
  and ab_prime_cin_prime (ab_prime_cin_prime_out, A, ~B, ~Cin);  // AND_Gate
  and a_prime_bcin_prime (a_prime_bcin_prime_out, ~A, B, ~Cin);  // AND_Gate
  and a_prime_b_prime_cin (a_prime_b_prime_cin_out, ~A, ~B, Cin);  // AND_Gate
  and acin (acin_out, A, Cin);
  and bcin (bcin_out, B, Cin);
  and ab (G, A, B);
  or a_b (P, A, B);
  or S_calc (S, abcin_out, ab_prime_cin_prime_out, a_prime_bcin_prime_out, a_prime_b_prime_cin_out);
  or cout_calc (Cout, acin_out, bcin_out, G);
endmodule

// CL
module CL_BLOCK (
  input  Pin0,
  input  Cin,
  input  Gin0,
  input  Pin1,
  input  Gin1,
  input  Pin2,
  input  Gin2,
  output C1,
  output Pout,
  output C2,
  output Gout,
  output C3___Cout
);

  wire p0cin_out, p1g0_out, p1pocin_out, p2g1_2_out, p2g1_out, p2p1g0_2_out, p2p1g0_out, p2p1p0cin_out;

  or u_c1 (C1, p0cin_out, Gin0);
  or u_c2 (C2, p1pocin_out, Gin1, p1g0_out);
  or c3 (C3___Cout, p2p1p0cin_out, p2p1g0_out, Gin2, p2g1_out);
  and p0cin (p0cin_out, Cin, Pin0);
  and p1pocin (p1pocin_out, Cin, Pin0, Pin1);
  and p1g0 (p1g0_out, Gin0, Pin1);
  and p2p1p0cin (p2p1p0cin_out, Pin0, Pin1, Pin2, Cin);
  and p2p1g0 (p2p1g0_out, Gin0, Pin1);
  and p2g1 (p2g1_out, Gin1, Pin2);
  and p2p1p0 (Pout, Pin0, Pin1, Pin2);
  and p2p1g0_2 (p2p1g0_2_out, Gin0, Pin1, Pin2);
  and p2g1_2 (p2g1_2_out, Gin1, Pin2);
  or u_gout (Gout, p2p1g0_2_out, p2g1_2_out, Gin2);
endmodule

// CLA 3bit
module CLA_PG3 (
  input  Cin,
  input  [2:0] In1,
  input  [2:0] In2,
  output [2:0] Out,
  output Pout,
  output Gout,
  output C3_Cout
);

  wire cl_block_1_c1, cl_block_1_c2, cla_pg1_1_g, cla_pg1_1_p, cla_pg1_2_g, cla_pg1_2_p, cla_pg1_3_g,
       cla_pg1_3_p;

  CLA_PG1 cla_pg1_1 (.A(In1[0]), .B(In2[0]), .Cin(Cin), .S(Out[0]), .P(cla_pg1_1_p), .G(cla_pg1_1_g));  // open: Cout
  CLA_PG1 cla_pg1_2 (
    .A(In1[1]), .B(In2[1]), .Cin(cl_block_1_c1), .S(Out[1]), .P(cla_pg1_2_p), .G(cla_pg1_2_g));  // open: Cout
  CLA_PG1 cla_pg1_3 (
    .A(In1[2]), .B(In2[2]), .Cin(cl_block_1_c2), .S(Out[2]), .P(cla_pg1_3_p), .G(cla_pg1_3_g));  // open: Cout
  CL_BLOCK cl_block_1 (
    .Pin0(cla_pg1_1_p), .Gin0(cla_pg1_1_g), .C1(cl_block_1_c1), .Pin1(cla_pg1_2_p), .Gin1(cla_pg1_2_g),
    .C2(cl_block_1_c2), .Pin2(cla_pg1_3_p), .Gin2(cla_pg1_3_g), .Cin(Cin), .C3___Cout(C3_Cout), .Pout(Pout),
    .Gout(Gout));
endmodule

// CLA 9bit
module CLA_PG9 (
  input  Cin,
  input  [8:0] In1,
  input  [8:0] In1_2,
  output [8:0] Out,
  output Pout,
  output Gout,
  output C3_Cout
);

  wire cl_block_1_c1, cl_block_1_c2, cla_pg3_1_gout, cla_pg3_1_pout, cla_pg3_2_gout, cla_pg3_2_pout,
       cla_pg3_3_gout, cla_pg3_3_pout;

  CLA_PG3 cla_pg3_1 (
    .In1(In1[2:0]), .In2(In1_2[2:0]), .Cin(Cin), .Out(Out[2:0]), .Pout(cla_pg3_1_pout), .Gout(cla_pg3_1_gout));  // open: C3_Cout
  CLA_PG3 cla_pg3_2 (
    .In1(In1[5:3]), .In2(In1_2[5:3]), .Cin(cl_block_1_c1), .Out(Out[5:3]), .Pout(cla_pg3_2_pout),
    .Gout(cla_pg3_2_gout));  // open: C3_Cout
  CLA_PG3 cla_pg3_3 (
    .In1(In1[8:6]), .In2(In1_2[8:6]), .Cin(cl_block_1_c2), .Out(Out[8:6]), .Pout(cla_pg3_3_pout),
    .Gout(cla_pg3_3_gout));  // open: C3_Cout
  CL_BLOCK cl_block_1 (
    .Pin0(cla_pg3_1_pout), .Gin0(cla_pg3_1_gout), .C1(cl_block_1_c1), .Pin1(cla_pg3_2_pout),
    .Gin1(cla_pg3_2_gout), .C2(cl_block_1_c2), .Pin2(cla_pg3_3_pout), .Gin2(cla_pg3_3_gout), .Cin(Cin),
    .C3___Cout(C3_Cout), .Pout(Pout), .Gout(Gout));
endmodule

module CLA_PG27 (
  input  Cin,
  input  [26:0] In1,
  input  [26:0] In2,
  output [26:0] Out,
  output Pout,
  output Gout,
  output C3_Cout
);

  wire cl_block_1_c1, cl_block_1_c2, cla_pg9_1_gout, cla_pg9_1_pout, cla_pg9_2_gout, cla_pg9_2_pout,
       cla_pg9_3_gout, cla_pg9_3_pout;

  CLA_PG9 cla_pg9_1 (
    .In1(In1[8:0]), .In1_2(In2[8:0]), .Cin(Cin), .Out(Out[8:0]), .Pout(cla_pg9_1_pout), .Gout(cla_pg9_1_gout));  // open: C3_Cout
  CLA_PG9 cla_pg9_2 (
    .In1(In1[17:9]), .In1_2(In2[17:9]), .Cin(cl_block_1_c1), .Out(Out[17:9]), .Pout(cla_pg9_2_pout),
    .Gout(cla_pg9_2_gout));  // open: C3_Cout
  CLA_PG9 cla_pg9_3 (
    .In1(In1[26:18]), .In1_2(In2[26:18]), .Cin(cl_block_1_c2), .Out(Out[26:18]), .Pout(cla_pg9_3_pout),
    .Gout(cla_pg9_3_gout));  // open: C3_Cout
  CL_BLOCK cl_block_1 (
    .Pin0(cla_pg9_1_pout), .Gin0(cla_pg9_1_gout), .C1(cl_block_1_c1), .Pin1(cla_pg9_2_pout),
    .Gin1(cla_pg9_2_gout), .C2(cl_block_1_c2), .Pin2(cla_pg9_3_pout), .Gin2(cla_pg9_3_gout), .Cin(Cin),
    .C3___Cout(C3_Cout), .Pout(Pout), .Gout(Gout));
endmodule
