// Logisim project 2Flop-2Wide-2Read-1Write.circ as structural Verilog: 1 circuit, main circuit 2Flop-2Wide-2Read-1Write
module _2Flop_2Wide_2Read_1Write (
  input  RegWrite,
  input  ReadReg1,
  input  ReadReg2,
  input  WriteReg,
  input  [1:0] WriteData,
  output [1:0] RegData1,
  output [1:0] RegData2
);

  wire and_1_out, and_2_out, Clock_out, decoder_1_out0, decoder_1_out1, or_1_out, or_2_out;
  wire [1:0] d_ff_1_q, d_ff_3_q;

  Decoder #(.enable("false")) decoder_1 (.out0(decoder_1_out0), .out1(decoder_1_out1), .sel(WriteReg));
  Clock Clock (.out(Clock_out));
  and and_1 (and_1_out, RegWrite, decoder_1_out0);
  and and_2 (and_2_out, decoder_1_out1, RegWrite);
  or or_1 (or_1_out, ~and_1_out, Clock_out);  // OR_Gate
  or or_2 (or_2_out, Clock_out, ~and_2_out);  // OR_Gate
  D_Flip_Flop #(.trigger("falling")) d_ff_1 (
    .clk(or_1_out), .D(WriteData[0]), .Q(d_ff_1_q[0]));  // open: Qn, preset, en, reset
  D_Flip_Flop #(.trigger("falling")) d_ff_2 (
    .clk(or_1_out), .D(WriteData[1]), .Q(d_ff_1_q[1]));  // open: Qn, preset, en, reset
  D_Flip_Flop #(.trigger("falling")) d_ff_3 (
    .clk(or_2_out), .D(WriteData[0]), .Q(d_ff_3_q[0]));  // open: Qn, preset, en, reset
  D_Flip_Flop #(.trigger("falling")) d_ff_4 (
    .clk(or_2_out), .D(WriteData[1]), .Q(d_ff_3_q[1]));  // open: Qn, preset, en, reset
  Multiplexer #(.width(2), .enable("false")) multiplexer_1 (
    .in0(d_ff_1_q), .in1(d_ff_3_q), .out(RegData1), .sel(ReadReg1));
  Multiplexer #(.width(2), .enable("false")) multiplexer_2 (
    .in0(d_ff_1_q), .in1(d_ff_3_q), .out(RegData2), .sel(ReadReg2));
endmodule
