// Logisim project 2Flop-2Wide-2Read.circ as structural Verilog: 1 circuit, main circuit main
module main (
  input  ReadReg1,
  input  ReadReg2,
  output [1:0] RegData1,
  output [1:0] RegData2
);

  wire Clock_out;
  wire [1:0] d_ff_1_q, d_ff_3_q;

  Clock Clock (.out(Clock_out));
  D_Flip_Flop #(.trigger("falling")) d_ff_1 (.clk(Clock_out), .Q(d_ff_1_q[0]));  // open: D, Qn, preset, en, reset
  D_Flip_Flop #(.trigger("falling")) d_ff_2 (.clk(Clock_out), .Q(d_ff_1_q[1]));  // open: D, Qn, preset, en, reset
  D_Flip_Flop #(.trigger("falling")) d_ff_3 (.clk(Clock_out), .Q(d_ff_3_q[0]));  // open: D, Qn, preset, en, reset
  D_Flip_Flop #(.trigger("falling")) d_ff_4 (.clk(Clock_out), .Q(d_ff_3_q[1]));  // open: D, Qn, preset, en, reset
  Multiplexer #(.width(2), .enable("false")) multiplexer_1 (
    .in0(d_ff_1_q), .in1(d_ff_3_q), .out(RegData1), .sel(ReadReg1));
  Multiplexer #(.width(2), .enable("false")) multiplexer_2 (
    .in0(d_ff_1_q), .in1(d_ff_3_q), .out(RegData2), .sel(ReadReg2));
endmodule
