// Logisim project 4Reg-32Wide-2Read-1Write.circ as structural Verilog: 1 circuit, main circuit 4Reg-32Wide-2Read-1Write
module _4Reg_32Wide_2Read_1Write (
  input  [1:0] ReadReg1,
  input  [1:0] ReadReg2,
  input  [1:0] WriteReg,
  input  [31:0] WriteData,
  input  RegWrite,
  output [31:0] ReadData1,
  output [31:0] ReadData2
);

  wire and_1_out, and_2_out, and_3_out, and_4_out, Clock_out, decoder_1_out0, decoder_1_out1, decoder_1_out2,
       decoder_1_out3;
  wire [31:0] register_1_q, register_2_q, register_3_q, register_4_q;

  Clock Clock (.out(Clock_out));
  Decoder #(.select(2), .enable("false")) decoder_1 (
    .out0(decoder_1_out0), .out1(decoder_1_out1), .out2(decoder_1_out2), .out3(decoder_1_out3), .sel(WriteReg));
  and and_1 (and_1_out, RegWrite, decoder_1_out0);
  and and_2 (and_2_out, RegWrite, decoder_1_out1);
  and and_3 (and_3_out, RegWrite, decoder_1_out2);
  and and_4 (and_4_out, RegWrite, decoder_1_out3);
  Register #(.width(32), .trigger("falling")) register_1 (
    .D(WriteData), .en(and_1_out), .Q(register_1_q), .clk(Clock_out));  // open: clr
  Register #(.width(32), .trigger("falling")) register_2 (
    .D(WriteData), .en(and_2_out), .Q(register_2_q), .clk(Clock_out));  // open: clr
  Register #(.width(32), .trigger("falling")) register_3 (
    .D(WriteData), .en(and_3_out), .Q(register_3_q), .clk(Clock_out));  // open: clr
  Register #(.width(32), .trigger("falling")) register_4 (
    .D(WriteData), .en(and_4_out), .Q(register_4_q), .clk(Clock_out));  // open: clr
  Multiplexer #(.select(2), .width(32), .enable("false")) multiplexer_1 (
    .in0(register_1_q), .in1(register_2_q), .in2(register_3_q), .in3(register_4_q), .out(ReadData1),
    .sel(ReadReg1));
  Multiplexer #(.select(2), .width(32), .enable("false")) multiplexer_2 (
    .in0(register_1_q), .in1(register_2_q), .in2(register_3_q), .in3(register_4_q), .out(ReadData2),
    .sel(ReadReg2));
endmodule
