// Logisim project alu-32bit-mips.circ as structural Verilog: 5 circuits, main circuit alu-32bit-mips
module alu_32bit_mips (
  input  Ainvert,
  input  Bnegate,
  input  [1:0] Oper,
  input  [31:0] A,
  input  [31:0] B,
  output Equal_Zero,
  output [31:0] Result,
  output Overflow,
  output CarryOut
);

  wire alu_1bit_slt_1_cout, alu_1bit_slt_2_cout, alu_1bit_slt_3_cout, alu_1bit_slt_4_cout,
       alu_1bit_slt_5_cout, alu_1bit_slt_6_cout, alu_1bit_slt_7_cout, alu_1bit_slt_8_cout,
       alu_1bit_slt_9_cout, alu_1bit_slt_10_cout, alu_1bit_slt_11_cout, alu_1bit_slt_12_cout,
       alu_1bit_slt_13_cout, alu_1bit_slt_14_cout, alu_1bit_slt_15_cout, alu_1bit_slt_16_cout,
       alu_1bit_slt_17_cout, alu_1bit_slt_18_cout, alu_1bit_slt_19_cout, alu_1bit_slt_20_cout,
       alu_1bit_slt_21_cout, alu_1bit_slt_22_cout, alu_1bit_slt_23_cout, alu_1bit_slt_24_cout,
       alu_1bit_slt_25_cout, alu_1bit_slt_26_cout, alu_1bit_slt_27_cout, alu_1bit_slt_28_cout,
       alu_1bit_slt_29_cout, alu_1bit_slt_30_cout, alu_1bit_slt_31_cout, alu_1bit_slt_32_set;

  alu_1bit_slt alu_1bit_slt_1 (
    .A(A[0]), .B(B[0]), .Less(alu_1bit_slt_32_set), .Ainvert(Ainvert), .Binvert(Bnegate), .Cin(Bnegate),
    .Op(Oper), .Cout(alu_1bit_slt_1_cout), .Result(Result[0]));  // open: Set, Overflow
  alu_1bit_slt alu_1bit_slt_2 (
    .A(A[1]), .B(B[1]), .Less(1'b0), .Ainvert(Ainvert), .Binvert(Bnegate), .Cin(alu_1bit_slt_1_cout),
    .Op(Oper), .Cout(alu_1bit_slt_2_cout), .Result(Result[1]));  // open: Set, Overflow
  alu_1bit_slt alu_1bit_slt_3 (
    .A(A[2]), .B(B[2]), .Less(1'b0), .Ainvert(Ainvert), .Binvert(Bnegate), .Cin(alu_1bit_slt_2_cout),
    .Op(Oper), .Cout(alu_1bit_slt_3_cout), .Result(Result[2]));  // open: Set, Overflow
  alu_1bit_slt alu_1bit_slt_4 (
    .A(A[3]), .B(B[3]), .Less(1'b0), .Ainvert(Ainvert), .Binvert(Bnegate), .Cin(alu_1bit_slt_3_cout),
    .Op(Oper), .Cout(alu_1bit_slt_4_cout), .Result(Result[3]));  // open: Set, Overflow
  alu_1bit_slt alu_1bit_slt_5 (
    .A(A[4]), .B(B[4]), .Less(1'b0), .Ainvert(Ainvert), .Binvert(Bnegate), .Cin(alu_1bit_slt_4_cout),
    .Op(Oper), .Cout(alu_1bit_slt_5_cout), .Result(Result[4]));  // open: Set, Overflow
  alu_1bit_slt alu_1bit_slt_6 (
    .A(A[5]), .B(B[5]), .Less(1'b0), .Ainvert(Ainvert), .Binvert(Bnegate), .Cin(alu_1bit_slt_5_cout),
    .Op(Oper), .Cout(alu_1bit_slt_6_cout), .Result(Result[5]));  // open: Set, Overflow
  alu_1bit_slt alu_1bit_slt_7 (
    .A(A[6]), .B(B[6]), .Less(1'b0), .Ainvert(Ainvert), .Binvert(Bnegate), .Cin(alu_1bit_slt_6_cout),
    .Op(Oper), .Cout(alu_1bit_slt_7_cout), .Result(Result[6]));  // open: Set, Overflow
  alu_1bit_slt alu_1bit_slt_8 (
    .A(A[7]), .B(B[7]), .Less(1'b0), .Ainvert(Ainvert), .Binvert(Bnegate), .Cin(alu_1bit_slt_7_cout),
    .Op(Oper), .Cout(alu_1bit_slt_8_cout), .Result(Result[7]));  // open: Set, Overflow
  alu_1bit_slt alu_1bit_slt_9 (
    .A(A[8]), .B(B[8]), .Less(1'b0), .Ainvert(Ainvert), .Binvert(Bnegate), .Cin(alu_1bit_slt_8_cout),
    .Op(Oper), .Cout(alu_1bit_slt_9_cout), .Result(Result[8]));  // open: Set, Overflow
  alu_1bit_slt alu_1bit_slt_10 (
    .A(A[9]), .B(B[9]), .Less(1'b0), .Ainvert(Ainvert), .Binvert(Bnegate), .Cin(alu_1bit_slt_9_cout),
    .Op(Oper), .Cout(alu_1bit_slt_10_cout), .Result(Result[9]));  // open: Set, Overflow
  alu_1bit_slt alu_1bit_slt_11 (
    .A(A[10]), .B(B[10]), .Less(1'b0), .Ainvert(Ainvert), .Binvert(Bnegate), .Cin(alu_1bit_slt_10_cout),
    .Op(Oper), .Cout(alu_1bit_slt_11_cout), .Result(Result[10]));  // open: Set, Overflow
  alu_1bit_slt alu_1bit_slt_12 (
    .A(A[11]), .B(B[11]), .Less(1'b0), .Ainvert(Ainvert), .Binvert(Bnegate), .Cin(alu_1bit_slt_11_cout),
    .Op(Oper), .Cout(alu_1bit_slt_12_cout), .Result(Result[11]));  // open: Set, Overflow
  alu_1bit_slt alu_1bit_slt_13 (
    .A(A[12]), .B(B[12]), .Less(1'b0), .Ainvert(Ainvert), .Binvert(Bnegate), .Cin(alu_1bit_slt_12_cout),
    .Op(Oper), .Cout(alu_1bit_slt_13_cout), .Result(Result[12]));  // open: Set, Overflow
  alu_1bit_slt alu_1bit_slt_14 (
    .A(A[13]), .B(B[13]), .Less(1'b0), .Ainvert(Ainvert), .Binvert(Bnegate), .Cin(alu_1bit_slt_13_cout),
    .Op(Oper), .Cout(alu_1bit_slt_14_cout), .Result(Result[13]));  // open: Set, Overflow
  alu_1bit_slt alu_1bit_slt_15 (
    .A(A[14]), .B(B[14]), .Less(1'b0), .Ainvert(Ainvert), .Binvert(Bnegate), .Cin(alu_1bit_slt_14_cout),
    .Op(Oper), .Cout(alu_1bit_slt_15_cout), .Result(Result[14]));  // open: Set, Overflow
  alu_1bit_slt alu_1bit_slt_16 (
    .A(A[15]), .B(B[15]), .Less(1'b0), .Ainvert(Ainvert), .Binvert(Bnegate), .Cin(alu_1bit_slt_15_cout),
    .Op(Oper), .Cout(alu_1bit_slt_16_cout), .Result(Result[15]));  // open: Set, Overflow
  alu_1bit_slt alu_1bit_slt_17 (
    .A(A[16]), .B(B[16]), .Less(1'b0), .Ainvert(Ainvert), .Binvert(Bnegate), .Cin(alu_1bit_slt_16_cout),
    .Op(Oper), .Cout(alu_1bit_slt_17_cout), .Result(Result[16]));  // open: Set, Overflow
  alu_1bit_slt alu_1bit_slt_18 (
    .A(A[17]), .B(B[17]), .Less(1'b0), .Ainvert(Ainvert), .Binvert(Bnegate), .Cin(alu_1bit_slt_17_cout),
    .Op(Oper), .Cout(alu_1bit_slt_18_cout), .Result(Result[17]));  // open: Set, Overflow
  alu_1bit_slt alu_1bit_slt_19 (
    .A(A[18]), .B(B[18]), .Less(1'b0), .Ainvert(Ainvert), .Binvert(Bnegate), .Cin(alu_1bit_slt_18_cout),
    .Op(Oper), .Cout(alu_1bit_slt_19_cout), .Result(Result[18]));  // open: Set, Overflow
  alu_1bit_slt alu_1bit_slt_20 (
    .A(A[19]), .B(B[19]), .Less(1'b0), .Ainvert(Ainvert), .Binvert(Bnegate), .Cin(alu_1bit_slt_19_cout),
    .Op(Oper), .Cout(alu_1bit_slt_20_cout), .Result(Result[19]));  // open: Set, Overflow
  alu_1bit_slt alu_1bit_slt_21 (
    .A(A[20]), .B(B[20]), .Less(1'b0), .Ainvert(Ainvert), .Binvert(Bnegate), .Cin(alu_1bit_slt_20_cout),
    .Op(Oper), .Cout(alu_1bit_slt_21_cout), .Result(Result[20]));  // open: Set, Overflow
  alu_1bit_slt alu_1bit_slt_22 (
    .A(A[21]), .B(B[21]), .Less(1'b0), .Ainvert(Ainvert), .Binvert(Bnegate), .Cin(alu_1bit_slt_21_cout),
    .Op(Oper), .Cout(alu_1bit_slt_22_cout), .Result(Result[21]));  // open: Set, Overflow
  alu_1bit_slt alu_1bit_slt_23 (
    .A(A[22]), .B(B[22]), .Less(1'b0), .Ainvert(Ainvert), .Binvert(Bnegate), .Cin(alu_1bit_slt_22_cout),
    .Op(Oper), .Cout(alu_1bit_slt_23_cout), .Result(Result[22]));  // open: Set, Overflow
  alu_1bit_slt alu_1bit_slt_24 (
    .A(A[23]), .B(B[23]), .Less(1'b0), .Ainvert(Ainvert), .Binvert(Bnegate), .Cin(alu_1bit_slt_23_cout),
    .Op(Oper), .Cout(alu_1bit_slt_24_cout), .Result(Result[23]));  // open: Set, Overflow
  alu_1bit_slt alu_1bit_slt_25 (
    .A(A[24]), .B(B[24]), .Less(1'b0), .Ainvert(Ainvert), .Binvert(Bnegate), .Cin(alu_1bit_slt_24_cout),
    .Op(Oper), .Cout(alu_1bit_slt_25_cout), .Result(Result[24]));  // open: Set, Overflow
  alu_1bit_slt alu_1bit_slt_26 (
    .A(A[25]), .B(B[25]), .Less(1'b0), .Ainvert(Ainvert), .Binvert(Bnegate), .Cin(alu_1bit_slt_25_cout),
    .Op(Oper), .Cout(alu_1bit_slt_26_cout), .Result(Result[25]));  // open: Set, Overflow
  alu_1bit_slt alu_1bit_slt_27 (
    .A(A[26]), .B(B[26]), .Less(1'b0), .Ainvert(Ainvert), .Binvert(Bnegate), .Cin(alu_1bit_slt_26_cout),
    .Op(Oper), .Cout(alu_1bit_slt_27_cout), .Result(Result[26]));  // open: Set, Overflow
  alu_1bit_slt alu_1bit_slt_28 (
    .A(A[27]), .B(B[27]), .Less(1'b0), .Ainvert(Ainvert), .Binvert(Bnegate), .Cin(alu_1bit_slt_27_cout),
    .Op(Oper), .Cout(alu_1bit_slt_28_cout), .Result(Result[27]));  // open: Set, Overflow
  alu_1bit_slt alu_1bit_slt_29 (
    .A(A[28]), .B(B[28]), .Less(1'b0), .Ainvert(Ainvert), .Binvert(Bnegate), .Cin(alu_1bit_slt_28_cout),
    .Op(Oper), .Cout(alu_1bit_slt_29_cout), .Result(Result[28]));  // open: Set, Overflow
  alu_1bit_slt alu_1bit_slt_30 (
    .A(A[29]), .B(B[29]), .Less(1'b0), .Ainvert(Ainvert), .Binvert(Bnegate), .Cin(alu_1bit_slt_29_cout),
    .Op(Oper), .Cout(alu_1bit_slt_30_cout), .Result(Result[29]));  // open: Set, Overflow
  alu_1bit_slt alu_1bit_slt_31 (
    .A(A[30]), .B(B[30]), .Less(1'b0), .Ainvert(Ainvert), .Binvert(Bnegate), .Cin(alu_1bit_slt_30_cout),
    .Op(Oper), .Cout(alu_1bit_slt_31_cout), .Result(Result[30]));  // open: Set, Overflow
  alu_1bit_slt alu_1bit_slt_32 (
    .A(A[31]), .B(B[31]), .Less(1'b0), .Ainvert(Ainvert), .Binvert(Bnegate), .Cin(alu_1bit_slt_31_cout),
    .Op(Oper), .Cout(CarryOut), .Result(Result[31]), .Set(alu_1bit_slt_32_set), .Overflow(Overflow));
  nor nor_1 (Equal_Zero, Result[0], Result[1], Result[2], Result[3], Result[4], Result[5], Result[6], Result[7], Result[8], Result[9], Result[10], Result[11], Result[12], Result[13], Result[14], Result[15], Result[16], Result[17], Result[18], Result[19], Result[20], Result[21], Result[22], Result[23], Result[24], Result[25], Result[26], Result[27], Result[28], Result[29], Result[30], Result[31]);

  // Notes on the sheet:
  //   Less
endmodule

// ALU
module alu_1bit_slt (
  input  Ainvert,
  input  Binvert,
  input  Cin,
  input  [1:0] Op,
  input  A,
  input  B,
  input  Less,
  output Result,
  output Set,
  output Overflow,
  output Cout
);

  wire adder_1bit_1_sum, and_1_out, mux_2_way_1_out, mux_2_way_2_out, not_1_out, not_2_out, or_1_out;

  not not_1 (not_1_out, A);
  not not_2 (not_2_out, B);
  mux_2_way mux_2_way_1 (.A(A), .B(not_1_out), .S(Ainvert), .OUT(mux_2_way_1_out));
  mux_2_way mux_2_way_2 (.A(B), .B(not_2_out), .S(Binvert), .OUT(mux_2_way_2_out));
  and and_1 (and_1_out, mux_2_way_1_out, mux_2_way_2_out);
  or or_1 (or_1_out, mux_2_way_1_out, mux_2_way_2_out);
  adder_1bit adder_1bit_1 (
    .A(mux_2_way_2_out), .B(mux_2_way_1_out), .CARRY_IN(Cin), .CARRRY_OUT(Cout), .SUM(adder_1bit_1_sum));
  mux_4_way mux_4_way_1 (
    .A(and_1_out), .B(or_1_out), .C(adder_1bit_1_sum), .D(Less), .S2(Op[1]), .S1(Op[0]), .OUT(Result));
  xor xor_1 (Overflow, Cin, Cout);
  xor xor_2 (Set, adder_1bit_1_sum, Overflow);
endmodule

// +
module adder_1bit (
  input  CARRY_IN,
  input  A,
  input  B,
  output SUM,
  output CARRRY_OUT
);

  wire and_1_out, and_2_out, xor_1_out;

  and and_1 (and_1_out, A, B);
  xor xor_1 (xor_1_out, A, B);
  and and_2 (and_2_out, xor_1_out, CARRY_IN);
  or or_1 (CARRRY_OUT, and_1_out, and_2_out);
  xor xor_2 (SUM, xor_1_out, CARRY_IN);
endmodule

// MUX
module mux_4_way (
  input  S2,
  input  S1,
  input  A,
  input  B,
  input  C,
  input  D,
  output OUT
);

  wire and_1_out, and_2_out, and_3_out, and_4_out;

  and and_1 (and_1_out, A, ~S1, ~S2);  // AND_Gate
  and and_2 (and_2_out, B, S1, ~S2);  // AND_Gate
  or or_1 (OUT, and_1_out, and_2_out, and_3_out, and_4_out);
  and and_3 (and_3_out, C, ~S1, S2);  // AND_Gate
  and and_4 (and_4_out, D, S1, S2);
endmodule

// MUX
module mux_2_way (
  input  S,
  input  A,
  input  B,
  output OUT
);

  wire and_1_out, and_2_out;

  and and_1 (and_1_out, A, ~S);  // AND_Gate
  and and_2 (and_2_out, B, S);
  or or_1 (OUT, and_1_out, and_2_out);
endmodule
