// Logisim project Adder-32.circ as structural Verilog: 1 circuit, main circuit Adder-32
module Adder_32 (
  input  [31:0] A,
  input  [31:0] B,
  output Equal_Zero,
  output [31:0] Result,
  output Overflow,
  output CarryOut
);

  wire alu_1bit_slt_1_cout, alu_1bit_slt_2_cout, alu_1bit_slt_3_cout, alu_1bit_slt_4_cout,
       alu_1bit_slt_5_cout, alu_1bit_slt_6_cout, alu_1bit_slt_7_cout, alu_1bit_slt_8_cout,
       alu_1bit_slt_9_cout, alu_1bit_slt_10_cout, alu_1bit_slt_11_cout, alu_1bit_slt_12_cout,
       alu_1bit_slt_13_cout, alu_1bit_slt_14_cout, alu_1bit_slt_15_cout, alu_1bit_slt_16_cout,
       alu_1bit_slt_17_cout, alu_1bit_slt_18_cout, alu_1bit_slt_19_cout, alu_1bit_slt_20_cout,
       alu_1bit_slt_21_cout, alu_1bit_slt_22_cout, alu_1bit_slt_23_cout, alu_1bit_slt_24_cout,
       alu_1bit_slt_25_cout, alu_1bit_slt_26_cout, alu_1bit_slt_27_cout, alu_1bit_slt_28_cout,
       alu_1bit_slt_29_cout, alu_1bit_slt_30_cout, alu_1bit_slt_31_cout, alu_1bit_slt_32_set;

  alu_1bit_slt alu_1bit_slt_1 (
    .A(A[0]), .B(B[0]), .Less(alu_1bit_slt_32_set), .Ainvert(1'b0), .Binvert(1'b0), .Cin(1'b0), .Op(2'b10),
    .Cout(alu_1bit_slt_1_cout), .Result(Result[0]));  // open: Set, Overflow
  alu_1bit_slt alu_1bit_slt_2 (
    .A(A[1]), .B(B[1]), .Less(1'b0), .Ainvert(1'b0), .Binvert(1'b0), .Cin(alu_1bit_slt_1_cout), .Op(2'b10),
    .Cout(alu_1bit_slt_2_cout), .Result(Result[1]));  // open: Set, Overflow
  alu_1bit_slt alu_1bit_slt_3 (
    .A(A[2]), .B(B[2]), .Less(1'b0), .Ainvert(1'b0), .Binvert(1'b0), .Cin(alu_1bit_slt_2_cout), .Op(2'b10),
    .Cout(alu_1bit_slt_3_cout), .Result(Result[2]));  // open: Set, Overflow
  alu_1bit_slt alu_1bit_slt_4 (
    .A(A[3]), .B(B[3]), .Less(1'b0), .Ainvert(1'b0), .Binvert(1'b0), .Cin(alu_1bit_slt_3_cout), .Op(2'b10),
    .Cout(alu_1bit_slt_4_cout), .Result(Result[3]));  // open: Set, Overflow
  alu_1bit_slt alu_1bit_slt_5 (
    .A(A[4]), .B(B[4]), .Less(1'b0), .Ainvert(1'b0), .Binvert(1'b0), .Cin(alu_1bit_slt_4_cout), .Op(2'b10),
    .Cout(alu_1bit_slt_5_cout), .Result(Result[4]));  // open: Set, Overflow
  alu_1bit_slt alu_1bit_slt_6 (
    .A(A[5]), .B(B[5]), .Less(1'b0), .Ainvert(1'b0), .Binvert(1'b0), .Cin(alu_1bit_slt_5_cout), .Op(2'b10),
    .Cout(alu_1bit_slt_6_cout), .Result(Result[5]));  // open: Set, Overflow
  alu_1bit_slt alu_1bit_slt_7 (
    .A(A[6]), .B(B[6]), .Less(1'b0), .Ainvert(1'b0), .Binvert(1'b0), .Cin(alu_1bit_slt_6_cout), .Op(2'b10),
    .Cout(alu_1bit_slt_7_cout), .Result(Result[6]));  // open: Set, Overflow
  alu_1bit_slt alu_1bit_slt_8 (
    .A(A[7]), .B(B[7]), .Less(1'b0), .Ainvert(1'b0), .Binvert(1'b0), .Cin(alu_1bit_slt_7_cout), .Op(2'b10),
    .Cout(alu_1bit_slt_8_cout), .Result(Result[7]));  // open: Set, Overflow
  alu_1bit_slt alu_1bit_slt_9 (
    .A(A[8]), .B(B[8]), .Less(1'b0), .Ainvert(1'b0), .Binvert(1'b0), .Cin(alu_1bit_slt_8_cout), .Op(2'b10),
    .Cout(alu_1bit_slt_9_cout), .Result(Result[8]));  // open: Set, Overflow
  alu_1bit_slt alu_1bit_slt_10 (
    .A(A[9]), .B(B[9]), .Less(1'b0), .Ainvert(1'b0), .Binvert(1'b0), .Cin(alu_1bit_slt_9_cout), .Op(2'b10),
    .Cout(alu_1bit_slt_10_cout), .Result(Result[9]));  // open: Set, Overflow
  alu_1bit_slt alu_1bit_slt_11 (
    .A(A[10]), .B(B[10]), .Less(1'b0), .Ainvert(1'b0), .Binvert(1'b0), .Cin(alu_1bit_slt_10_cout),
    .Op(2'b10), .Cout(alu_1bit_slt_11_cout), .Result(Result[10]));  // open: Set, Overflow
  alu_1bit_slt alu_1bit_slt_12 (
    .A(A[11]), .B(B[11]), .Less(1'b0), .Ainvert(1'b0), .Binvert(1'b0), .Cin(alu_1bit_slt_11_cout),
    .Op(2'b10), .Cout(alu_1bit_slt_12_cout), .Result(Result[11]));  // open: Set, Overflow
  alu_1bit_slt alu_1bit_slt_13 (
    .A(A[12]), .B(B[12]), .Less(1'b0), .Ainvert(1'b0), .Binvert(1'b0), .Cin(alu_1bit_slt_12_cout),
    .Op(2'b10), .Cout(alu_1bit_slt_13_cout), .Result(Result[12]));  // open: Set, Overflow
  alu_1bit_slt alu_1bit_slt_14 (
    .A(A[13]), .B(B[13]), .Less(1'b0), .Ainvert(1'b0), .Binvert(1'b0), .Cin(alu_1bit_slt_13_cout),
    .Op(2'b10), .Cout(alu_1bit_slt_14_cout), .Result(Result[13]));  // open: Set, Overflow
  alu_1bit_slt alu_1bit_slt_15 (
    .A(A[14]), .B(B[14]), .Less(1'b0), .Ainvert(1'b0), .Binvert(1'b0), .Cin(alu_1bit_slt_14_cout),
    .Op(2'b10), .Cout(alu_1bit_slt_15_cout), .Result(Result[14]));  // open: Set, Overflow
  alu_1bit_slt alu_1bit_slt_16 (
    .A(A[15]), .B(B[15]), .Less(1'b0), .Ainvert(1'b0), .Binvert(1'b0), .Cin(alu_1bit_slt_15_cout),
    .Op(2'b10), .Cout(alu_1bit_slt_16_cout), .Result(Result[15]));  // open: Set, Overflow
  alu_1bit_slt alu_1bit_slt_17 (
    .A(A[16]), .B(B[16]), .Less(1'b0), .Ainvert(1'b0), .Binvert(1'b0), .Cin(alu_1bit_slt_16_cout),
    .Op(2'b10), .Cout(alu_1bit_slt_17_cout), .Result(Result[16]));  // open: Set, Overflow
  alu_1bit_slt alu_1bit_slt_18 (
    .A(A[17]), .B(B[17]), .Less(1'b0), .Ainvert(1'b0), .Binvert(1'b0), .Cin(alu_1bit_slt_17_cout),
    .Op(2'b10), .Cout(alu_1bit_slt_18_cout), .Result(Result[17]));  // open: Set, Overflow
  alu_1bit_slt alu_1bit_slt_19 (
    .A(A[18]), .B(B[18]), .Less(1'b0), .Ainvert(1'b0), .Binvert(1'b0), .Cin(alu_1bit_slt_18_cout),
    .Op(2'b10), .Cout(alu_1bit_slt_19_cout), .Result(Result[18]));  // open: Set, Overflow
  alu_1bit_slt alu_1bit_slt_20 (
    .A(A[19]), .B(B[19]), .Less(1'b0), .Ainvert(1'b0), .Binvert(1'b0), .Cin(alu_1bit_slt_19_cout),
    .Op(2'b10), .Cout(alu_1bit_slt_20_cout), .Result(Result[19]));  // open: Set, Overflow
  alu_1bit_slt alu_1bit_slt_21 (
    .A(A[20]), .B(B[20]), .Less(1'b0), .Ainvert(1'b0), .Binvert(1'b0), .Cin(alu_1bit_slt_20_cout),
    .Op(2'b10), .Cout(alu_1bit_slt_21_cout), .Result(Result[20]));  // open: Set, Overflow
  alu_1bit_slt alu_1bit_slt_22 (
    .A(A[21]), .B(B[21]), .Less(1'b0), .Ainvert(1'b0), .Binvert(1'b0), .Cin(alu_1bit_slt_21_cout),
    .Op(2'b10), .Cout(alu_1bit_slt_22_cout), .Result(Result[21]));  // open: Set, Overflow
  alu_1bit_slt alu_1bit_slt_23 (
    .A(A[22]), .B(B[22]), .Less(1'b0), .Ainvert(1'b0), .Binvert(1'b0), .Cin(alu_1bit_slt_22_cout),
    .Op(2'b10), .Cout(alu_1bit_slt_23_cout), .Result(Result[22]));  // open: Set, Overflow
  alu_1bit_slt alu_1bit_slt_24 (
    .A(A[23]), .B(B[23]), .Less(1'b0), .Ainvert(1'b0), .Binvert(1'b0), .Cin(alu_1bit_slt_23_cout),
    .Op(2'b10), .Cout(alu_1bit_slt_24_cout), .Result(Result[23]));  // open: Set, Overflow
  alu_1bit_slt alu_1bit_slt_25 (
    .A(A[24]), .B(B[24]), .Less(1'b0), .Ainvert(1'b0), .Binvert(1'b0), .Cin(alu_1bit_slt_24_cout),
    .Op(2'b10), .Cout(alu_1bit_slt_25_cout), .Result(Result[24]));  // open: Set, Overflow
  alu_1bit_slt alu_1bit_slt_26 (
    .A(A[25]), .B(B[25]), .Less(1'b0), .Ainvert(1'b0), .Binvert(1'b0), .Cin(alu_1bit_slt_25_cout),
    .Op(2'b10), .Cout(alu_1bit_slt_26_cout), .Result(Result[25]));  // open: Set, Overflow
  alu_1bit_slt alu_1bit_slt_27 (
    .A(A[26]), .B(B[26]), .Less(1'b0), .Ainvert(1'b0), .Binvert(1'b0), .Cin(alu_1bit_slt_26_cout),
    .Op(2'b10), .Cout(alu_1bit_slt_27_cout), .Result(Result[26]));  // open: Set, Overflow
  alu_1bit_slt alu_1bit_slt_28 (
    .A(A[27]), .B(B[27]), .Less(1'b0), .Ainvert(1'b0), .Binvert(1'b0), .Cin(alu_1bit_slt_27_cout),
    .Op(2'b10), .Cout(alu_1bit_slt_28_cout), .Result(Result[27]));  // open: Set, Overflow
  alu_1bit_slt alu_1bit_slt_29 (
    .A(A[28]), .B(B[28]), .Less(1'b0), .Ainvert(1'b0), .Binvert(1'b0), .Cin(alu_1bit_slt_28_cout),
    .Op(2'b10), .Cout(alu_1bit_slt_29_cout), .Result(Result[28]));  // open: Set, Overflow
  alu_1bit_slt alu_1bit_slt_30 (
    .A(A[29]), .B(B[29]), .Less(1'b0), .Ainvert(1'b0), .Binvert(1'b0), .Cin(alu_1bit_slt_29_cout),
    .Op(2'b10), .Cout(alu_1bit_slt_30_cout), .Result(Result[29]));  // open: Set, Overflow
  alu_1bit_slt alu_1bit_slt_31 (
    .A(A[30]), .B(B[30]), .Less(1'b0), .Ainvert(1'b0), .Binvert(1'b0), .Cin(alu_1bit_slt_30_cout),
    .Op(2'b10), .Cout(alu_1bit_slt_31_cout), .Result(Result[30]));  // open: Set, Overflow
  alu_1bit_slt alu_1bit_slt_32 (
    .A(A[31]), .B(B[31]), .Less(1'b0), .Ainvert(1'b0), .Binvert(1'b0), .Cin(alu_1bit_slt_31_cout),
    .Op(2'b10), .Cout(CarryOut), .Result(Result[31]), .Set(alu_1bit_slt_32_set), .Overflow(Overflow));
  nor nor_1 (Equal_Zero, Result[0], Result[1], Result[2], Result[3], Result[4], Result[5], Result[6], Result[7], Result[8], Result[9], Result[10], Result[11], Result[12], Result[13], Result[14], Result[15], Result[16], Result[17], Result[18], Result[19], Result[20], Result[21], Result[22], Result[23], Result[24], Result[25], Result[26], Result[27], Result[28], Result[29], Result[30], Result[31]);

  // Notes on the sheet:
  //   Ainverse
  //   Bnegate
  //   Less
  //   Oper
endmodule
