// Logisim project Data-Memory.circ as structural Verilog: 1 circuit, main circuit Data-Memory
module Data_Memory (
  input  [31:0] Address,
  input  [31:0] WriteData,
  input  MemWrite,
  input  Clock,
  output [31:0] ReadData
);

  wire not_1_out;

  not not_1 (not_1_out, Clock);
  RAM #(.dataWidth(32), .bus("separate")) ram_1 (
    .addr(Address[9:2]), .din(WriteData), .data(ReadData), .str(MemWrite), .clk(not_1_out));  // open: sel, ld, clr
endmodule
