// Logisim project Datapath.circ as structural Verilog: 1 circuit, main circuit Datapath
module Datapath (
);

  wire alu_32bit_mips_1_equal_zero, and_1_out, clock_1_out, main_control_1_alusrc, main_control_1_branch,
       main_control_1_memtoreg, main_control_1_memwrite, main_control_1_regdst, main_control_1_regwrite;
  wire [1:0] main_control_1_aluop0;
  wire [2:0] alu_control_1_alucntl;
  wire [4:0] multiplexer_1_out;
  wire [31:0] adder_32_1_result, adder_32_2_result, alu_32bit_mips_1_result, data_memory_1_readdata,
       instruction_memory_1_instruction, multiplexer_2_out, multiplexer_3_out, multiplexer_4_out,
       pc_1_dataoutput, registers_1_readdata1, registers_1_readdata2, shift_left_1_instruction_2,
       sign_extend_1_instruction_2;

  Clock clock_1 (.out(clock_1_out));
  PC pc_1 (.DataInput(multiplexer_4_out), .Clock(clock_1_out), .DataOutput(pc_1_dataoutput));
  Instruction_Memory instruction_memory_1 (
    .ReadAddress(pc_1_dataoutput), .Instruction(instruction_memory_1_instruction));
  Adder_32 adder_32_1 (
    .B(pc_1_dataoutput), .A(32'h4), .Result(adder_32_1_result));  // open: CarryOut, Equal_Zero, Overflow
  Main_Control main_control_1 (
    .Instruction(instruction_memory_1_instruction[31:26]), .RegDst(main_control_1_regdst),
    .ALUSrc(main_control_1_alusrc), .MemToReg(main_control_1_memtoreg), .RegWrite(main_control_1_regwrite),
    .MemWrite(main_control_1_memwrite), .Branch(main_control_1_branch), .ALUOp1(main_control_1_aluop0[1]),
    .ALUOp0(main_control_1_aluop0[0]));
  Multiplexer #(.width(5), .enable("false")) multiplexer_1 (
    .in0(instruction_memory_1_instruction[20:16]), .in1(instruction_memory_1_instruction[15:11]),
    .out(multiplexer_1_out), .sel(main_control_1_regdst));
  Sign_Extend sign_extend_1 (
    .Instruction(instruction_memory_1_instruction[15:0]), .Instruction_2(sign_extend_1_instruction_2));
  Registers registers_1 (
    .ReadRegister1(instruction_memory_1_instruction[22:21]),
    .ReadRegister2(instruction_memory_1_instruction[17:16]), .WriteRegister(multiplexer_1_out[1:0]),
    .WriteData(multiplexer_2_out), .Clock(clock_1_out), .RegWrite(main_control_1_regwrite),
    .ReadData1(registers_1_readdata1), .ReadData2(registers_1_readdata2));
  ALU_Control alu_control_1 (
    .Instruction(instruction_memory_1_instruction[5:0]), .ALUOp(main_control_1_aluop0),
    .ALUCntl(alu_control_1_alucntl));
  Multiplexer #(.width(32), .enable("false")) multiplexer_2 (
    .in0(alu_32bit_mips_1_result), .in1(data_memory_1_readdata), .out(multiplexer_2_out),
    .sel(main_control_1_memtoreg));
  Shift_Left shift_left_1 (.Instruction(sign_extend_1_instruction_2), .Instruction_2(shift_left_1_instruction_2));
  Multiplexer #(.width(32), .enable("false")) multiplexer_3 (
    .in0(registers_1_readdata2), .in1(sign_extend_1_instruction_2), .out(multiplexer_3_out),
    .sel(main_control_1_alusrc));
  Adder_32 adder_32_2 (
    .B(adder_32_1_result), .A(shift_left_1_instruction_2), .Result(adder_32_2_result));  // open: CarryOut, Equal_Zero, Overflow
  alu_32bit_mips alu_32bit_mips_1 (
    .B(multiplexer_3_out), .Ainvert(1'b0), .Bnegate(alu_control_1_alucntl[2]),
    .Oper(alu_control_1_alucntl[1:0]), .A(registers_1_readdata1), .Equal_Zero(alu_32bit_mips_1_equal_zero),
    .Result(alu_32bit_mips_1_result));  // open: CarryOut, Overflow
  Multiplexer #(.width(32), .enable("false")) multiplexer_4 (
    .in0(adder_32_1_result), .in1(adder_32_2_result), .out(multiplexer_4_out), .sel(and_1_out));
  and and_1 (and_1_out, main_control_1_branch, alu_32bit_mips_1_equal_zero);
  Data_Memory data_memory_1 (
    .Address(alu_32bit_mips_1_result), .WriteData(registers_1_readdata2), .MemWrite(main_control_1_memwrite),
    .Clock(clock_1_out), .ReadData(data_memory_1_readdata));
endmodule
