// Logisim project Main-Control.circ as structural Verilog: 1 circuit, main circuit Main-Control
module Main_Control (
  input  [5:0] Instruction,
  output RegDst,
  output ALUSrc,
  output MemToReg,
  output RegWrite,
  output MemWrite,
  output Branch,
  output ALUOp1,
  output ALUOp0
);

  and and_1 (ALUOp1, ~Instruction[5], ~Instruction[4], ~Instruction[3], ~Instruction[2], ~Instruction[1], ~Instruction[0]);  // AND_Gate
  and and_2 (MemToReg, Instruction[5], ~Instruction[4], ~Instruction[3], ~Instruction[2], Instruction[1], Instruction[0]);  // AND_Gate
  and and_3 (MemWrite, Instruction[5], ~Instruction[4], Instruction[3], ~Instruction[2], Instruction[1], Instruction[0]);  // AND_Gate
  and and_4 (ALUOp0, ~Instruction[5], ~Instruction[4], ~Instruction[3], Instruction[2], ~Instruction[1], ~Instruction[0]);  // AND_Gate
  or or_1 (ALUSrc, MemToReg, MemWrite);
  or or_2 (RegWrite, ALUOp1, MemToReg);

  assign Branch = ALUOp0;
  assign RegDst = ALUOp1;
endmodule
