// Logisim project Shift-Left.circ as structural Verilog: 1 circuit, main circuit Shift-Left
module Shift_Left (
  input  [31:0] Instruction,
  output [31:0] Instruction_2
);

  Shifter #(.width(32)) shifter_1 (.in(Instruction), .\dist (5'b00010), .out(Instruction_2));
endmodule
