// Logisim project ALU-Control.circ as structural Verilog: 1 circuit, main circuit ALU-Control
module ALU_Control (
  input  [1:0] ALUOp,
  input  [5:0] Instruction,
  output [2:0] ALUCntl
);

  wire and_1_out, or_1_out;

  and and_1 (and_1_out, ALUOp[1], Instruction[1]);
  or or_1 (or_1_out, Instruction[3], Instruction[0]);
  or or_2 (ALUCntl[2], ALUOp[0], and_1_out);
  or or_3 (ALUCntl[1], ~ALUOp[1], ~Instruction[2]);  // OR_Gate
  and and_2 (ALUCntl[0], ALUOp[1], or_1_out);
endmodule
