// Logisim project Instruction-Memory.circ as structural Verilog: 1 circuit, main circuit Instruction-Memory
module Instruction_Memory (
  input  [31:0] ReadAddress,
  output [31:0] Instruction
);

  ROM #(.addrWidth(6), .dataWidth(32)) rom_1 (.addr(ReadAddress[7:2]), .data(Instruction));  // open: sel

  // Notes on the sheet:
  //   contents of rom_1 (hex, n*v repeats v):
  //   22 210822 421022 8c030000 230820 411020 8c030004 10230001 1000fffa ac020008 1000ffff
endmodule
