// Logisim project PC.circ as structural Verilog: 1 circuit, main circuit PC
module PC (
  input  [31:0] DataInput,
  input  Clock,
  output [31:0] DataOutput
);

  Register #(.width(32), .trigger("falling")) register_1 (.D(DataInput), .Q(DataOutput), .clk(Clock));  // open: en, clr
endmodule
