// Logisim project Sign-Extend.circ as structural Verilog: 1 circuit, main circuit Sign-Extend
module Sign_Extend (
  input  [15:0] Instruction,
  output [31:0] Instruction_2
);

  assign Instruction_2 = {{16{Instruction[15]}}, Instruction};  // Bit_Extender bit_extender_1
endmodule
