// Logisim project mux-demux.circ as structural Verilog: 1 circuit, main circuit main
module main (
  input  MSB,
  input  LSB,
  input  A,
  input  B,
  input  C,
  input  D,
  output A_2,
  output X,
  output B_2,
  output C_2,
  output D_2
);

  wire _00_out, _01_out, _10_out, _11_out, not_1_out, not_2_out, not_3_out, not_4_out;

  not not_1 (not_1_out, MSB);
  not not_2 (not_2_out, LSB);
  and _00 (_00_out, not_2_out, not_1_out, A);
  and _01 (_01_out, not_1_out, LSB, B);
  and _10 (_10_out, MSB, not_2_out, C);
  and _11 (_11_out, LSB, MSB, D);
  or or_1 (X, _00_out, _01_out, _10_out, _11_out);
  not not_3 (not_3_out, MSB);
  not not_4 (not_4_out, LSB);
  and _00_2 (A_2, not_4_out, not_3_out, X);
  and _01_2 (B_2, not_3_out, LSB, X);
  and _10_2 (C_2, MSB, not_4_out, X);
  and _11_2 (D_2, LSB, MSB, X);

  // Notes on the sheet:
  //   Address
  //   4 to 1 Multiplexer
  //   Data
  //   www.learnabout-electronics.org
  //   1 to 4 De-multiplexer
endmodule
